# Fritzing sketch LED_receiver_ESP8266_only_rev1 (saved by Fritzing 0.9.3b)
breadboards: 1

parts:
  Part1 = Breadboard Power Supply Board SMD
  U1 = NodeMCU V1.0
  Part2 = LED Matrix - Serial Interface - Red/Green/Blue
  Part3 = LED Matrix - Serial Interface - Red/Green/Blue  # not connected
  Part4 = LED Matrix - Serial Interface - Red/Green/Blue  # not connected
  Part5 = LED Matrix - Serial Interface - Red/Green/Blue  # not connected

nets:
  GND: Part1.GND, Part1.VIN
  VCC: Part1.VCC, Part2.VCC
  N1: U1.D5, Part2.SCK
  N2: U1.D6, Part2.CS
  N3: U1.D7, Part2.MISO

notes:
  Use a wall plug to provide power for the LED matrix through the breadboard power supply.
  You'll need to provide power to the ESP8266 separately.
  NodeMCU D5 to LED CLK
  NodeMCU D6 to LED LOAD
  NodeMCU D7 to LED DATA IN

custom parts:
  NodeMCU V1.0: ESP8266 based NodeMCU
