# Fritzing sketch esp8266_arduino_comm_test (saved by Fritzing 0.9.3b)

parts:
  Part2 = Arduino Uno (Rev3)
  U2 = NodeMCU V1.0

nets:
  N1: Part2.D8, U2.TX
  N2: Part2.D9_PWM, U2.RX
  GND: Part2.GND, U2.GND
  N3: Part2.3V3, U2.EN

notes:
  - Pull up EN(CH_PD) to 3v3
  - Supply power separately
  to each microcontroller!
  - Don't bother trying to drive ESP8266 off 3v3 from an Arduino. It's a power hog. Give it its own supply!

custom parts:
  NodeMCU V1.0: ESP8266 based NodeMCU
